// Logisim project latchb.circ as structural Verilog: 1 circuit, main circuit LATCH8
module LATCH8 (
  input  [7:0] D,
  input  WE,
  output [7:0] Q
);

  wire not_1_out, not_2_out, not_3_out, not_4_out, not_5_out, not_6_out, not_7_out, not_8_out;
  wire [7:0] controlled_buffer_1_out;

  assign controlled_buffer_1_out = WE ? D : 8'bz;  // Controlled_Buffer controlled_buffer_1
  S_R_Flip_Flop s_r_ff_1 (.Q(Q[0]), .reset(not_1_out), .preset(controlled_buffer_1_out[0]));  // open: S, R, clk, Qn
  not not_1 (not_1_out, controlled_buffer_1_out[0]);
  S_R_Flip_Flop s_r_ff_2 (.Q(Q[4]), .reset(not_2_out), .preset(controlled_buffer_1_out[4]));  // open: S, R, clk, Qn
  not not_2 (not_2_out, controlled_buffer_1_out[4]);
  S_R_Flip_Flop s_r_ff_3 (.Q(Q[1]), .reset(not_3_out), .preset(controlled_buffer_1_out[1]));  // open: S, R, clk, Qn
  not not_3 (not_3_out, controlled_buffer_1_out[1]);
  S_R_Flip_Flop s_r_ff_4 (.Q(Q[5]), .reset(not_4_out), .preset(controlled_buffer_1_out[5]));  // open: S, R, clk, Qn
  not not_4 (not_4_out, controlled_buffer_1_out[5]);
  S_R_Flip_Flop s_r_ff_5 (.Q(Q[2]), .reset(not_5_out), .preset(controlled_buffer_1_out[2]));  // open: S, R, clk, Qn
  not not_5 (not_5_out, controlled_buffer_1_out[2]);
  S_R_Flip_Flop s_r_ff_6 (.Q(Q[6]), .reset(not_6_out), .preset(controlled_buffer_1_out[6]));  // open: S, R, clk, Qn
  not not_6 (not_6_out, controlled_buffer_1_out[6]);
  S_R_Flip_Flop s_r_ff_7 (.Q(Q[3]), .reset(not_7_out), .preset(controlled_buffer_1_out[3]));  // open: S, R, clk, Qn
  not not_7 (not_7_out, controlled_buffer_1_out[3]);
  S_R_Flip_Flop s_r_ff_8 (.Q(Q[7]), .reset(not_8_out), .preset(controlled_buffer_1_out[7]));  // open: S, R, clk, Qn
  not not_8 (not_8_out, controlled_buffer_1_out[7]);
endmodule
